# Fritzing sketch secuencia 6 leds_ece (saved by Fritzing 0.9.3b)
breadboards: 1

parts:
  Parte1 = Arduino Uno (Rev3)
  R1 = Resistor [tolerance=±5% resistance=220 package=THT]
  LED4 = LED - 5mm [color="Red (633nm)" package="5 mm [THT]"]
  R2 = Resistor [tolerance=±5% resistance=220 package=THT]
  R3 = Resistor [tolerance=±5% resistance=220 package=THT]
  LED9 = LED - 5mm [color="Red (633nm)" package="5 mm [THT]"]
  LED5 = smd LED [color="Yellow (585nm)" package="1206 [SMD]"]
  LED6 = smd LED [color="Green (555nm)" package="1206 [SMD]"]
  R5 = Resistor [tolerance=±5% resistance=220 package=THT]
  R6 = Resistor [tolerance=±5% resistance=220 package=THT]
  LED8 = smd LED [color="Yellow (585nm)" package="1206 [SMD]"]
  LED7 = smd LED [color="Green (555nm)" package="1206 [SMD]"]
  R4 = Resistor [tolerance=±5% resistance=220 package=THT]

nets:
  N1: Parte1.D8, LED8.anode
  N2: Parte1.D9_PWM, LED9.anode
  N3: Parte1.D4, LED4.anode
  N4: Parte1.D5_PWM, LED5.anode
  N5: Parte1.D6_PWM, LED6.anode
  N6: Parte1.D7, LED7.anode
  N7: Parte1.GND, R1.Pin_1, R2.Pin_1, R3.Pin_1, R5.Pin_1, R6.Pin_1, R4.Pin_1
  N8: R1.Pin_0, LED4.cathode
  N9: R2.Pin_0, LED5.cathode
  N10: R3.Pin_0, LED6.cathode
  N11: LED9.cathode, R6.Pin_0
  N12: R5.Pin_0, LED8.cathode
  N13: LED7.cathode, R4.Pin_0
